// Logisim project Kathleen16.circ as structural Verilog: 5 circuits, main circuit main
// dataout
module main (
);

  wire Clock, EnableWrite, isADDIorLWorSW, isSWorBEQ, MemWrite, Reset, ZF;
  wire [1:0] ctrl, InSrc;
  wire [2:0] ctrlALU, multiplexer_2_out, ra, rb, rc;
  wire [6:0] imm7;
  wire [9:0] imm10;
  wire [15:0] bit_extender_1_out, datain, dataout, destjALR, extenseur_1_out_3, multiplexer_1_out,
       multiplexer_3_out, pc, pc_1, rom_1_data, ual_1_ual;

  Button button_1 (.out(Clock));
  Button button_2 (.out(Reset));
  extenseur extenseur_1 (.in_2(imm10), .out_3(extenseur_1_out_3));  // open: in_1
  RAM #(.addrWidth(16), .dataWidth(16), .bus("separate")) ram_1 (
    .addr(ual_1_ual), .din(datain), .data(dataout), .str(MemWrite), .clk(Clock), .clr(Reset));  // open: sel, ld
  Multiplexer #(.select(2), .width(16)) multiplexer_1 (
    .in0(extenseur_1_out_3), .in1(pc_1), .in2(dataout), .in3(ual_1_ual), .out(multiplexer_1_out), .sel(InSrc));  // open: en
  assign bit_extender_1_out = {{9{imm7[6]}}, imm7};  // Bit_Extender bit_extender_1
  Multiplexer #(.width(3)) multiplexer_2 (.in0(rc), .in1(ra), .out(multiplexer_2_out), .sel(isSWorBEQ));  // open: en
  BancDeRegistre bancderegistre_1 (
    .B_exit(datain), .C_or_A(destjALR), .Reset(Reset), .Clock(Clock), .EnableWrite(EnableWrite),
    .InputValue(multiplexer_1_out), .rb(rb), .ra(ra), .rc(multiplexer_2_out));  // open: isWhoreBEQ
  IFU IFU (
    .ZF(ZF), .DestjALR(destjALR), .pc(rom_1_data), .clock(Clock), .reset(Reset), .InSrc(InSrc), .Imm7(imm7),
    .Imm10(imm10), .rc(rc), .rb(rb), .ra(ra), .ctrlALU(ctrl), .MemWrite(MemWrite), .isSWorBEQ(isSWorBEQ),
    .EnableWrite(EnableWrite), .isADDIorLWorSW(isADDIorLWorSW), .pc_2(pc), .pc_1(pc_1));
  Multiplexer #(.width(16)) multiplexer_3 (
    .in0(datain), .in1(bit_extender_1_out), .out(multiplexer_3_out), .sel(isADDIorLWorSW));  // open: en
  ROM #(.addrWidth(16), .dataWidth(16)) rom_1 (.addr(pc), .data(rom_1_data));  // open: sel
  UAL ual_1 (.v1(destjALR), .v2(multiplexer_3_out), .ctrlALU(ctrlALU), .ZF(ZF), .UAL(ual_1_ual));
endmodule

module extenseur (
  input  [5:0] in_1,
  input  [9:0] in_2,
  output [15:0] out_3
);


  assign out_3 = {in_2, in_1};
endmodule

module BancDeRegistre (
  input  [2:0] rb,
  input  [2:0] ra,
  input  [2:0] rc,
  input  [15:0] InputValue,
  input  EnableWrite,
  input  isWhoreBEQ,
  input  Reset,
  input  Clock,
  output [15:0] B_exit,
  output [15:0] C_or_A
);

  wire decoder_1_out0, decoder_1_out1, decoder_1_out2, decoder_1_out3, decoder_1_out4, decoder_1_out5,
       decoder_1_out6, decoder_1_out7;
  wire [2:0] multiplexer_3_out, rc_t;
  wire [15:0] _1, _2, _3, _4, _5, _6, _7, _8;

  Decoder #(.select(3), .disabled(0)) decoder_1 (
    .out0(decoder_1_out0), .out1(decoder_1_out1), .out2(decoder_1_out2), .out3(decoder_1_out3),
    .out4(decoder_1_out4), .out5(decoder_1_out5), .out6(decoder_1_out6), .out7(decoder_1_out7), .sel(ra),
    .en(EnableWrite));
  Register #(.width(16)) u__1 (.D(InputValue), .en(decoder_1_out0), .Q(_1), .clk(Clock), .clr(Reset));
  Register #(.width(16)) u__2 (.D(InputValue), .en(decoder_1_out1), .Q(_2), .clk(Clock), .clr(Reset));
  Register #(.width(16)) u__3 (.D(InputValue), .en(decoder_1_out2), .Q(_3), .clk(Clock), .clr(Reset));
  Register #(.width(16)) u__4 (.D(InputValue), .en(decoder_1_out3), .Q(_4), .clk(Clock), .clr(Reset));
  Register #(.width(16)) u__5 (.D(InputValue), .en(decoder_1_out4), .Q(_5), .clk(Clock), .clr(Reset));
  Register #(.width(16)) u__6 (.D(InputValue), .en(decoder_1_out5), .Q(_6), .clk(Clock), .clr(Reset));
  Register #(.width(16)) u__7 (.D(InputValue), .en(decoder_1_out6), .Q(_7), .clk(Clock), .clr(Reset));
  Register #(.width(16)) u__8 (.D(InputValue), .en(decoder_1_out7), .Q(_8), .clk(Clock), .clr(Reset));
  Multiplexer #(.select(3), .width(16)) multiplexer_1 (
    .in0(_1), .in1(_2), .in2(_3), .in3(_4), .in4(_5), .in5(_6), .in6(_7), .in7(_8), .out(B_exit), .sel(rb));  // open: en
  Multiplexer #(.select(3), .width(16)) multiplexer_2 (
    .in0(_1), .in1(_2), .in2(_3), .in3(_4), .in4(_5), .in5(_6), .in6(_7), .in7(_8), .out(C_or_A),
    .sel(multiplexer_3_out));  // open: en
  Multiplexer #(.width(3)) multiplexer_3 (.in0(rc_t), .in1(ra), .out(multiplexer_3_out), .sel(isWhoreBEQ));  // open: en

  assign rc = ra;

  // Other names for the same wires on the sheet: BExit[15:0] = B_exit; Exit[15:0] = C_or_A
endmodule

module UAL (
  input  [15:0] v1,
  input  [15:0] v2,
  input  [2:0] ctrlALU,
  output ZF,
  output [15:0] UAL
);

  wire c_minus, c_plus, cf;
  wire [15:0] adder_1_out, nand_1_out, subtractor_1_out;

  Adder #(.width(16)) adder_1 (.a(v1), .b(v2), .out(adder_1_out), .cin(1'b0), .cout(c_plus));
  Subtractor #(.width(16)) subtractor_1 (.a(v1), .b(v2), .out(subtractor_1_out), .bin(1'b0), .bout(c_minus));
  assign nand_1_out = ~v1;  // NAND_Gate nand_1, 16 bits wide NAND_Gate
  Multiplexer #(.select(3)) multiplexer_1 (
    .in0(c_plus), .in1(c_minus), .in2(1'b0), .in3(1'b0), .in4(1'b0), .in5(1'b0), .in6(1'b0), .in7(1'b0),
    .out(cf), .sel(ctrlALU));  // open: en
  Multiplexer #(.select(3), .width(16)) multiplexer_2 (
    .in0(adder_1_out), .in1(subtractor_1_out), .in2(nand_1_out), .in7({16{1'b0}}), .out(UAL), .sel(ctrlALU));  // open: in3, in4, in5, in6, en
  nor nor_1 (ZF, UAL[0], UAL[1], UAL[2], UAL[3], UAL[4], UAL[5], UAL[6], UAL[7], UAL[8], UAL[9], UAL[10], UAL[11], UAL[12], UAL[13], UAL[14], UAL[15]);

  // Other names for the same wires on the sheet: ctrl[2:0] = ctrlALU
endmodule

module IFU (
  input  [9:0] Imm10,
  input  ZF,
  input  clock,
  input  reset,
  input  [6:0] Imm7,
  input  [15:0] DestjALR,
  input  [15:0] pc,
  output [2:0] rc,
  output [2:0] rb,
  output [2:0] ra,
  output [1:0] ctrlALU,
  output MemWrite,
  output isSWorBEQ,
  output EnableWrite,
  output isADDIorLWorSW,
  output [15:0] pc_2,
  output [15:0] pc_1,
  output [1:0] InSrc
);

  wire add, addi, and_1_out, beq, jalr, lui, lw, \nand , not_1_out, not_2_out, not_3_out, or_1_out, RRI, RRR;
  wire [6:0] Imm7_t;
  wire [6:3] demultiplexer_2_out0;
  wire [9:0] demultiplexer_1_out0;
  wire [15:0] adder_1_out, adder_2_out, bit_extender_1_out, multiplexer_1_out, register_1_q;

  not not_1 (not_1_out, DestjALR[13]);
  Demultiplexer #(.width(10)) demultiplexer_1 (
    .out0(demultiplexer_1_out0), .out1(Imm10), .in(DestjALR[9:0]), .en(lui));  // open: sel
  not not_2 (not_2_out, DestjALR[14]);
  Demultiplexer #(.width(10)) demultiplexer_2 (
    .out0({rb, demultiplexer_2_out0, rc}), .out1({rb, Imm7_t}), .in(demultiplexer_1_out0), .en(RRI));  // open: sel
  not not_3 (not_3_out, DestjALR[15]);
  and u_add (add, not_1_out, not_2_out, not_3_out);
  and u_addi (addi, not_1_out, not_2_out, DestjALR[15]);
  and u_nand (\nand , not_1_out, DestjALR[14], not_3_out);
  and u_lui (lui, not_1_out, DestjALR[14], DestjALR[15]);
  and sw (MemWrite, DestjALR[13], not_2_out, not_3_out);
  and u_lw (lw, DestjALR[13], not_2_out, DestjALR[15]);
  and u_beq (beq, DestjALR[13], DestjALR[14], not_3_out);
  and u_jalr (jalr, DestjALR[13], DestjALR[14], DestjALR[15]);
  or or_1 (or_1_out, add, addi);
  or or_2 (RRI, jalr, beq, lw, MemWrite, addi);
  or or_3 (RRR, add, \nand );
  or or_4 (isSWorBEQ, MemWrite, beq);
  or or_5 (EnableWrite, jalr, add, lw, lui, \nand , addi);
  or or_6 (isADDIorLWorSW, addi, lw, MemWrite);
  Priority_Encoder #(.select(2)) priority_encoder_1 (
    .in0(lui), .in1(jalr), .in2(lw), .in3(add), .out(InSrc));  // open: gs, en_out, en_in
  Register #(.width(16)) register_1 (.D(pc), .Q(register_1_q), .clk(clock), .clr(reset));  // open: en
  Priority_Encoder #(.select(2)) priority_encoder_2 (
    .in0(or_1_out), .in1(beq), .in2(\nand ), .out(ctrlALU));  // open: in3, gs, en_out, en_in
  Adder #(.width(16)) adder_1 (.a(register_1_q), .b(16'h1), .out(adder_1_out));  // open: cin, cout
  assign bit_extender_1_out = {{9{1'b0}}, Imm7};  // Bit_Extender bit_extender_1
  Adder #(.width(16)) adder_2 (.a(adder_1_out), .b(bit_extender_1_out), .out(adder_2_out));  // open: cin, cout
  Adder #(.width(16)) adder_3 (.a(pc), .b(16'h1), .out(pc_1));  // open: cin, cout
  Multiplexer #(.width(16)) multiplexer_1 (
    .in0(adder_1_out), .in1(adder_2_out), .out(multiplexer_1_out), .sel(and_1_out));  // open: en
  and and_1 (and_1_out, beq, ZF);
  Multiplexer #(.width(16)) multiplexer_2 (.in0(DestjALR), .in1(multiplexer_1_out), .out(pc), .sel(jalr));  // open: en

  assign pc_2 = pc;

  // Other names for the same wires on the sheet: RI = lui; reg_A[2:0] = DestjALR[12:10]; sw = MemWrite
endmodule
